// Logisim project ETFStudent.circ as structural Verilog: 13 circuits, main circuit REG32_LD
module REG32_LD (
  input  [31:0] I15__0,
  input  LD,
  input  mr,
  input  CLK,
  output [31:0] A15__0
);

  // REG16_LD reg16_ld_1: pin names not known; wires that end beside it: CLK, mr, I15__0[31:16], A15__0[31:16], LD
  // REG16_LD reg16_ld_2: pin names not known; wires that end beside it: CLK, mr, I15__0[15:0], A15__0[15:0], LD

  // Notes on the sheet:
  //   __
endmodule

module KMADR (
  input  immed,
  input  memdir,
  input  memind,
  input  regind,
  input  preincr,
  input  postdec,
  input  regdir,
  output [7:0] Adr6__0
);

  assign Adr6__0 = immed ? 8'h2 : 8'bz;  // Controlled_Buffer controlled_buffer_1
  assign Adr6__0 = memdir ? 8'h3 : 8'bz;  // Controlled_Buffer controlled_buffer_2
  assign Adr6__0 = memind ? 8'h4 : 8'bz;  // Controlled_Buffer controlled_buffer_3
  assign Adr6__0 = regind ? 8'hc : 8'bz;  // Controlled_Buffer controlled_buffer_4
  assign Adr6__0 = preincr ? 8'hd : 8'bz;  // Controlled_Buffer controlled_buffer_5
  assign Adr6__0 = postdec ? 8'h11 : 8'bz;  // Controlled_Buffer controlled_buffer_6
  assign Adr6__0 = regdir ? 8'h15 : 8'bz;  // Controlled_Buffer controlled_buffer_7
endmodule

module KMOPR (
  input  LD,
  input  ST,
  input  ADD,
  input  OR,
  input  DEC,
  input  BGREU,
  input  BLSSU,
  input  BLEQU,
  input  JGRT,
  input  JLEQ,
  input  JMP,
  input  JSR,
  input  POPPSW,
  input  RTI,
  input  RTS,
  input  PUSHPSW,
  input  ROR,
  input  RORC,
  input  STIVTP,
  input  STRFIND,
  input  HALT,
  output [5:0] Adr5__0
);

  assign Adr5__0 = LD ? 6'b000010 : 6'bz;  // Controlled_Buffer controlled_buffer_1
  assign Adr5__0 = ST ? 6'b000100 : 6'bz;  // Controlled_Buffer controlled_buffer_2
  assign Adr5__0 = ADD ? 6'b001011 : 6'bz;  // Controlled_Buffer controlled_buffer_3
  assign Adr5__0 = OR ? 6'b001101 : 6'bz;  // Controlled_Buffer controlled_buffer_4
  assign Adr5__0 = DEC ? 6'b001111 : 6'bz;  // Controlled_Buffer controlled_buffer_5
  assign Adr5__0 = BGREU ? 6'b010001 : 6'bz;  // Controlled_Buffer controlled_buffer_6
  assign Adr5__0 = BLSSU ? 6'b010001 : 6'bz;  // Controlled_Buffer controlled_buffer_7
  assign Adr5__0 = BLEQU ? 6'b010001 : 6'bz;  // Controlled_Buffer controlled_buffer_8
  assign Adr5__0 = JGRT ? 6'b010011 : 6'bz;  // Controlled_Buffer controlled_buffer_9
  assign Adr5__0 = JLEQ ? 6'b010011 : 6'bz;  // Controlled_Buffer controlled_buffer_10
  assign Adr5__0 = JMP ? 6'b010100 : 6'bz;  // Controlled_Buffer controlled_buffer_11
  assign Adr5__0 = JSR ? 6'b010101 : 6'bz;  // Controlled_Buffer controlled_buffer_12
  assign Adr5__0 = POPPSW ? 6'b011010 : 6'bz;  // Controlled_Buffer controlled_buffer_13
  assign Adr5__0 = RTI ? 6'b011010 : 6'bz;  // Controlled_Buffer controlled_buffer_14
  assign Adr5__0 = RTS ? 6'b100010 : 6'bz;  // Controlled_Buffer controlled_buffer_15
  assign Adr5__0 = PUSHPSW ? 6'b101010 : 6'bz;  // Controlled_Buffer controlled_buffer_16
  assign Adr5__0 = ROR ? 6'b101111 : 6'bz;  // Controlled_Buffer controlled_buffer_17
  assign Adr5__0 = RORC ? 6'b110001 : 6'bz;  // Controlled_Buffer controlled_buffer_18
  assign Adr5__0 = STIVTP ? 6'b110011 : 6'bz;  // Controlled_Buffer controlled_buffer_19
  assign Adr5__0 = STRFIND ? 6'b110100 : 6'bz;  // Controlled_Buffer controlled_buffer_20
  assign Adr5__0 = HALT ? 6'b111101 : 6'bz;  // Controlled_Buffer controlled_buffer_21
endmodule

module REG6_INC_LD (
  input  [5:0] I5__0,
  input  LD,
  input  INC,
  input  mr,
  input  CLK,
  output [5:0] A5__0
);

  wire reg2m_inc_ld_1_p7, reg2m_inc_ld_2_p8;

  // REG2m_INC_LD reg2m_inc_ld_1: pin names not known; wires that end beside it: CLK, mr, I5__0[5:4], A5__0[5:4], LD, INC, reg2m_inc_ld_1_p7
  // REG2m_INC_LD reg2m_inc_ld_2: pin names not known; wires that end beside it: CLK, reg2m_inc_ld_1_p7, mr, I5__0[3:2], A5__0[3:2], LD, INC, reg2m_inc_ld_2_p8
  // REG2m_INC_LD reg2m_inc_ld_3: pin names not known; wires that end beside it: CLK, reg2m_inc_ld_2_p8, mr, I5__0[1:0], A5__0[1:0], LD, INC, INC

  // Notes on the sheet:
  //   __
endmodule

module DEMUX1_2 (
  input  in_1,
  input  in_2,
  output out_3,
  output out_4
);

  wire not_1_out;

  not not_1 (not_1_out, in_1);
  and and_1 (out_3, in_2, not_1_out);
  and and_2 (out_4, in_1, in_2);
endmodule

module ROM256x24 (
  input  [7:0] A7__0,
  input  CS,
  output [23:0] DOUT
);

  ROM #(.dataWidth(24)) rom_1 (.addr(A7__0), .data(DOUT), .sel(CS));
endmodule

module GPR16x16 (
  input  [15:0] DI15__0,
  input  [3:0] A3__0,
  input  WR,
  input  CLK,
  output [15:0] DO15__0
);

  wire and_2_out, and_13_out, CS0, CS1, CS2, CS3, CS4, CS5, CS6, CS7, CS8, CS9, CS10, CS11, CS12, CS13, CS14,
       CS15, reg16_ld_1_p4, reg16_ld_3_p4, reg16_ld_4_p4, reg16_ld_5_p4, reg16_ld_6_p4, reg16_ld_7_p4,
       reg16_ld_8_p4, reg16_ld_9_p4, reg16_ld_10_p4, reg16_ld_11_p4, reg16_ld_12_p4, reg16_ld_14_p4,
       reg16_ld_15_p4, reg16_ld_16_p4;
  wire [15:0] reg16_ld_1_p3, reg16_ld_2_p3, reg16_ld_3_p3, reg16_ld_4_p3, reg16_ld_5_p3, reg16_ld_6_p3,
       reg16_ld_7_p3, reg16_ld_8_p3, reg16_ld_9_p3, reg16_ld_10_p3, reg16_ld_11_p3, reg16_ld_12_p3,
       reg16_ld_13_p3, reg16_ld_14_p3, reg16_ld_15_p3, reg16_ld_16_p3;

  // DC4_16 dc4_16_1: pin names not known; wires that end beside it: A3__0, 1'b1, CS0, CS1, CS2, CS3, CS4, CS5, CS6, CS7, CS8, CS9, CS10, CS11, CS12, CS13, CS14, CS15
  // REG16_LD reg16_ld_1: pin names not known; wires that end beside it: CLK, DI15__0, reg16_ld_1_p3, reg16_ld_1_p4
  and and_1 (reg16_ld_1_p4, CS0, WR);
  assign DO15__0 = CS0 ? reg16_ld_1_p3 : 16'bz;  // Controlled_Buffer controlled_buffer_1
  and and_2 (and_2_out, CS1, WR);
  // REG16_LD reg16_ld_2: pin names not known; wires that end beside it: CLK, DI15__0, reg16_ld_2_p3, and_2_out
  assign DO15__0 = CS1 ? reg16_ld_2_p3 : 16'bz;  // Controlled_Buffer controlled_buffer_2
  // REG16_LD reg16_ld_3: pin names not known; wires that end beside it: CLK, DI15__0, reg16_ld_3_p3, reg16_ld_3_p4
  and and_3 (reg16_ld_3_p4, CS2, WR);
  assign DO15__0 = CS2 ? reg16_ld_3_p3 : 16'bz;  // Controlled_Buffer controlled_buffer_3
  // REG16_LD reg16_ld_4: pin names not known; wires that end beside it: CLK, DI15__0, reg16_ld_4_p3, reg16_ld_4_p4
  and and_4 (reg16_ld_4_p4, CS3, WR);
  assign DO15__0 = CS3 ? reg16_ld_4_p3 : 16'bz;  // Controlled_Buffer controlled_buffer_4
  // REG16_LD reg16_ld_5: pin names not known; wires that end beside it: CLK, DI15__0, reg16_ld_5_p3, reg16_ld_5_p4
  assign DO15__0 = CS4 ? reg16_ld_5_p3 : 16'bz;  // Controlled_Buffer controlled_buffer_5
  // REG16_LD reg16_ld_6: pin names not known; wires that end beside it: CLK, DI15__0, reg16_ld_6_p3, reg16_ld_6_p4
  assign DO15__0 = CS5 ? reg16_ld_6_p3 : 16'bz;  // Controlled_Buffer controlled_buffer_6
  // REG16_LD reg16_ld_7: pin names not known; wires that end beside it: CLK, DI15__0, reg16_ld_7_p3, reg16_ld_7_p4
  assign DO15__0 = CS6 ? reg16_ld_7_p3 : 16'bz;  // Controlled_Buffer controlled_buffer_7
  // REG16_LD reg16_ld_8: pin names not known; wires that end beside it: CLK, DI15__0, reg16_ld_8_p3, reg16_ld_8_p4
  assign DO15__0 = CS7 ? reg16_ld_8_p3 : 16'bz;  // Controlled_Buffer controlled_buffer_8
  and and_5 (reg16_ld_5_p4, CS4, WR);
  and and_6 (reg16_ld_6_p4, CS5, WR);
  and and_7 (reg16_ld_7_p4, CS6, WR);
  and and_8 (reg16_ld_8_p4, CS7, WR);
  // REG16_LD reg16_ld_9: pin names not known; wires that end beside it: CLK, DI15__0, reg16_ld_9_p3, reg16_ld_9_p4
  assign DO15__0 = CS8 ? reg16_ld_9_p3 : 16'bz;  // Controlled_Buffer controlled_buffer_9
  // REG16_LD reg16_ld_10: pin names not known; wires that end beside it: CLK, DI15__0, reg16_ld_10_p3, reg16_ld_10_p4
  assign DO15__0 = CS9 ? reg16_ld_10_p3 : 16'bz;  // Controlled_Buffer controlled_buffer_10
  // REG16_LD reg16_ld_11: pin names not known; wires that end beside it: CLK, DI15__0, reg16_ld_11_p3, reg16_ld_11_p4
  assign DO15__0 = CS10 ? reg16_ld_11_p3 : 16'bz;  // Controlled_Buffer controlled_buffer_11
  // REG16_LD reg16_ld_12: pin names not known; wires that end beside it: CLK, DI15__0, reg16_ld_12_p3, reg16_ld_12_p4
  assign DO15__0 = CS11 ? reg16_ld_12_p3 : 16'bz;  // Controlled_Buffer controlled_buffer_12
  and and_9 (reg16_ld_9_p4, CS8, WR);
  and and_10 (reg16_ld_10_p4, CS9, WR);
  and and_11 (reg16_ld_11_p4, CS10, WR);
  and and_12 (reg16_ld_12_p4, CS11, WR);
  and and_13 (and_13_out, CS12, WR);
  // REG16_LD reg16_ld_13: pin names not known; wires that end beside it: CLK, DI15__0, reg16_ld_13_p3, and_13_out
  assign DO15__0 = CS12 ? reg16_ld_13_p3 : 16'bz;  // Controlled_Buffer controlled_buffer_13
  // REG16_LD reg16_ld_14: pin names not known; wires that end beside it: CLK, DI15__0, reg16_ld_14_p3, reg16_ld_14_p4
  and and_14 (reg16_ld_14_p4, CS13, WR);
  assign DO15__0 = CS13 ? reg16_ld_14_p3 : 16'bz;  // Controlled_Buffer controlled_buffer_14
  // REG16_LD reg16_ld_15: pin names not known; wires that end beside it: CLK, DI15__0, reg16_ld_15_p3, reg16_ld_15_p4
  and and_15 (reg16_ld_15_p4, CS14, WR);
  assign DO15__0 = CS14 ? reg16_ld_15_p3 : 16'bz;  // Controlled_Buffer controlled_buffer_15
  // REG16_LD reg16_ld_16: pin names not known; wires that end beside it: CLK, DI15__0, reg16_ld_16_p3, reg16_ld_16_p4
  and and_16 (reg16_ld_16_p4, CS15, WR);
  assign DO15__0 = CS15 ? reg16_ld_16_p3 : 16'bz;  // Controlled_Buffer controlled_buffer_16

  // Other names for the same wires on the sheet: inREG[15:0] = DI15__0; outREG[15:0] = DO15__0
endmodule

module ROM256x26 (
  input  [7:0] A7__0,
  input  CS,
  output [25:0] DOUT
);

  ROM #(.dataWidth(26)) rom_1 (.addr(A7__0), .data(DOUT), .sel(CS));
endmodule

module OR16b (
  input  [15:0] A15__0,
  input  [15:0] B15__0,
  output [15:0] DOUT
);

  or or_1 (DOUT[0], A15__0[0], B15__0[0]);
  or or_2 (DOUT[1], B15__0[1], A15__0[1]);
  or or_3 (DOUT[2], B15__0[2], A15__0[2]);
  or or_4 (DOUT[3], B15__0[3], A15__0[3]);
  or or_5 (DOUT[4], B15__0[4], A15__0[4]);
  or or_6 (DOUT[5], B15__0[5], A15__0[5]);
  or or_7 (DOUT[6], B15__0[6], A15__0[6]);
  or or_8 (DOUT[7], B15__0[7], A15__0[7]);
  or or_9 (DOUT[8], B15__0[8], A15__0[8]);
  or or_10 (DOUT[9], B15__0[9], A15__0[9]);
  or or_11 (DOUT[10], B15__0[10], A15__0[10]);
  or or_12 (DOUT[11], B15__0[11], A15__0[11]);
  or or_13 (DOUT[12], B15__0[12], A15__0[12]);
  or or_14 (DOUT[13], B15__0[13], A15__0[13]);
  or or_15 (DOUT[14], B15__0[14], A15__0[14]);
  or or_16 (DOUT[15], B15__0[15], A15__0[15]);
endmodule

module ROR (
  input  [15:0] input_A,
  output carryROR,
  output [15:0] output_A
);


  assign carryROR = input_A[0];
  assign output_A = {input_A[0], input_A[15:1]};
endmodule

module RORC (
  input  [15:0] inputA,
  input  PSWC,
  output outputC,
  output [15:0] outputA
);


  assign outputA = {PSWC, inputA[15:1]};
  assign outputC = inputA[0];
endmodule

module ROM64x46 (
  input  [5:0] A5__0,
  input  CS,
  output [31:0] DOUT31__0,
  output [13:0] DOUT45__32
);

  ROM #(.addrWidth(6), .dataWidth(14)) rom_1 (.addr(A5__0), .data(DOUT45__32), .sel(CS));
  ROM #(.addrWidth(6), .dataWidth(32)) rom_2 (.addr(A5__0), .data(DOUT31__0), .sel(CS));
endmodule

module ROM64x26 (
  input  [5:0] A5__0,
  input  CS,
  output [25:0] DOUT
);

  ROM #(.addrWidth(6), .dataWidth(26)) rom_1 (.addr(A5__0), .data(DOUT), .sel(CS));
endmodule
