// Logisim project ORT2Project.circ as structural Verilog: 8 circuits, main circuit COMPUTER
module COMPUTER (
);

  wire BTN_RST_out, CLK, cpu_1_inta, interrupt_interface_4_1_p4, interrupt_interface_4_1_p5,
       interrupt_interface_4_1_p6, interrupt_interface_4_1_p7, pull_resistor_3_node, pull_resistor_5_node,
       ram_1_out_8, rst;
  wire [1:0] cpu_1_uext1__0;
  wire [3:0] interrupt_interface_4_1_p1;
  wire [7:0] pull_resistor_2_node, ram_1_out_7;
  wire [15:0] pull_resistor_4_node;

  Button BTN_RST (.out(BTN_RST_out));
  Clock u_CLK (.out(CLK));
  // RisingEdge risingedge_1: pin names not known; wires that end beside it: BTN_RST_out, CLK, rst
  RAM ram_1 (
    .in_1(pull_resistor_4_node), .in_2(CLK), .in_3(pull_resistor_2_node), .in_4(pull_resistor_3_node),
    .in_5(pull_resistor_5_node), .in_6(rst), .out_7(ram_1_out_7), .out_8(ram_1_out_8));
  Pull_Resistor pull_resistor_1 (.node(ram_1_out_7));
  Pull_Resistor pull_resistor_2 (.node(pull_resistor_2_node));
  Pull_Resistor pull_resistor_3 (.node(pull_resistor_3_node));
  Pull_Resistor pull_resistor_4 (.node(pull_resistor_4_node));
  Pull_Resistor pull_resistor_5 (.node(pull_resistor_5_node));
  Pull_Resistor pull_resistor_6 (.node(ram_1_out_8));
  CPU cpu_1 (
    .in_1(rst), .in_2(CLK), .in_3(ram_1_out_8), .in_4(ram_1_out_7), .ABUS(pull_resistor_4_node),
    .DOUTBUS(pull_resistor_2_node), .out_8(pull_resistor_3_node), .out_9(pull_resistor_5_node),
    .inta(cpu_1_inta), .intr3__0(interrupt_interface_4_1_p1), .UEXT1__0(cpu_1_uext1__0));
  // INTERRUPT_INTERFACE_4 interrupt_interface_4_1: pin names not known; wires that end beside it: interrupt_interface_4_1_p1, cpu_1_inta, cpu_1_uext1__0, interrupt_interface_4_1_p4, interrupt_interface_4_1_p5, interrupt_interface_4_1_p6, interrupt_interface_4_1_p7, CLK
  Button BTN_INTR3 (.out(interrupt_interface_4_1_p4));
  Button BTN_INTR2 (.out(interrupt_interface_4_1_p5));
  Button BTN_INTR1 (.out(interrupt_interface_4_1_p6));
  Button BTN_INTR0 (.out(interrupt_interface_4_1_p7));
endmodule

module CPU (
  input  in_1,
  input  in_2,
  input  in_3,
  input  [7:0] in_4,
  input  [3:0] intr3__0,
  output [15:0] ABUS,
  output [7:0] DOUTBUS,
  output out_8,
  output out_9,
  output inta,
  output [1:0] UEXT1__0
);

  wire [3:0] common_1_phaseffbus;
  wire [6:0] common_1_addrbus, pull_resistor_2_node;
  wire [7:0] A, ALU, B, pull_resistor_7_node;
  wire [14:0] pull_resistor_5_node;
  wire [15:0] INTRADDR, PSW;
  wire [17:0] pull_resistor_6_node;
  wire [20:0] common_1_instrucbus;

  COMMON common_1 (
    .CLK(in_2), .RST(in_1), .DIN(in_4), .CMEMBUS(pull_resistor_5_node), .MAR_2(ABUS), .MDR_2(DOUTBUS),
    .PHASEFFBUS(common_1_phaseffbus), .INSTRUCBUS(common_1_instrucbus), .ADDRBUS(common_1_addrbus),
    .PSW(PSW), .CREGBUS(pull_resistor_6_node), .CFFBUS(pull_resistor_7_node), .B(B), .A(A),
    .CPSW(pull_resistor_2_node), .ALU(ALU), .IVTPPDSP(INTRADDR));  // open: PC, MAR, MDR, PC_2, Akumulator, Sabirac, Oduzimac, Signali, out_21, out_26
  Pull_Resistor pull_resistor_1 (.node(common_1_phaseffbus));
  Pull_Resistor pull_resistor_2 (.node(pull_resistor_2_node));
  Pull_Resistor pull_resistor_3 (.node(common_1_instrucbus));
  Pull_Resistor pull_resistor_4 (.node(common_1_addrbus));
  Pull_Resistor pull_resistor_5 (.node(pull_resistor_5_node));
  Pull_Resistor pull_resistor_6 (.node(pull_resistor_6_node));
  Pull_Resistor pull_resistor_7 (.node(pull_resistor_7_node));
  FETCH fetch_1 (
    .in_1(in_1), .in_2(in_2), .in_3(in_3), .PHASEFFBUS(common_1_phaseffbus),
    .INSTRUCBUS(common_1_instrucbus), .ADDRBUS(common_1_addrbus), .PSW(PSW), .rdMEM(out_9),
    .CMEMBUS(pull_resistor_5_node), .CFFBUS(pull_resistor_7_node), .CREGBUS(pull_resistor_6_node));
  ADDR addr_1 (
    .in_1(in_1), .in_2(in_2), .in_3(in_3), .PHASEFFBUS(common_1_phaseffbus),
    .INSTRUCBUS(common_1_instrucbus), .ADDRBUS(common_1_addrbus), .rdMEM(out_9),
    .CMEMBUS(pull_resistor_5_node), .CFFBUS(pull_resistor_7_node), .CREGBUS(pull_resistor_6_node));
  EXEC exec_1 (
    .in_1(in_1), .in_2(in_2), .in_3(in_3), .B(B), .PHASEFFBUS(common_1_phaseffbus),
    .INSTRUCBUS(common_1_instrucbus), .ADDRBUS(common_1_addrbus), .PSW(PSW), .A(A), .ALU(ALU),
    .CMEMBUS(pull_resistor_5_node), .CFFBUS(pull_resistor_7_node), .CREGBUS(pull_resistor_6_node),
    .CPSW(pull_resistor_2_node), .rdMEM(out_9), .wrMEM(out_8));  // open: Signali, Akumulator, Sabirac, Oduzimac, in_5, in_6
  INTR intr_1 (
    .in_1(in_1), .in_2(in_2), .in_3(in_3), .PHASEFFBUS(common_1_phaseffbus),
    .INSTRUCBUS(common_1_instrucbus), .PSW(PSW), .intr(intr3__0), .ADDIVTP(INTRADDR),
    .CMEMBUS(pull_resistor_5_node), .CFFBUS(pull_resistor_7_node), .CREGBUS(pull_resistor_6_node),
    .rdMEM(out_9), .wrMEM(out_8), .UEXT1__0(UEXT1__0), .inta(inta));  // open: in_8

  // Other names for the same wires on the sheet: CLK = in_2; DIN7__0[7:0] = in_4; FCBUS = in_3; MAR[15:0] = ABUS;
  //   MDR[7:0] = DOUTBUS; RD = out_9; rst = in_1; WR = out_8
endmodule

module COMMON (
  input  CLK,
  input  RST,
  input  [7:0] DIN,
  input  [7:0] A,
  input  [7:0] ALU,
  input  [15:0] IVTPPDSP,
  input  [15:0] PC,
  input  [15:0] MAR,
  input  [7:0] MDR,
  input  [15:0] Akumulator,
  input  [15:0] Sabirac,
  input  [15:0] Oduzimac,
  input  [3:0] Signali,
  input  [14:0] CMEMBUS,
  input  [7:0] CFFBUS,
  input  [17:0] CREGBUS,
  input  [6:0] CPSW,
  output [15:0] PC_2,
  output [15:0] MAR_2,
  output [7:0] MDR_2,
  output [15:0] out_21,
  output [3:0] PHASEFFBUS,
  output [20:0] INSTRUCBUS,
  output [6:0] ADDRBUS,
  output [15:0] PSW,
  output [15:0] out_26,
  output [7:0] B
);

  wire adresneinstr, adrinst, and_10_out, and_11_out, and_12_out, and_13_out, and_14_out, and_15_out,
       and_16_out, and_17_out, and_18_out, and_19_out, and_20_out, and_21_out, and_22_out, and_23_out,
       and_24_out, and_25_out, and_26_out, and_27_out, and_28_out, and_29_out, and_30_out, and_31_out,
       and_32_out, and_33_out, and_34_out, and_35_out, and_36_out, and_37_out, and_38_out, and_39_out,
       and_40_out, and_41_out, bezadrinst, branchinst, jmpinst, mp2_16b_1_p3, mp4_16b_1_p5, mp4_16b_2_p5,
       mp8_8b_1_p8, mp8_16b_1_p8, not_1_out, not_3_out, not_6_out, not_11_out, or_2_out, or_3_out, or_4_out,
       or_5_out, or_6_out, or_7_out, or_8_out, or_9_out, or_10_out, or_11_out, or_12_out, or_13_out,
       or_14_out, or_15_out, or_16_out, outCNTB, reg8_ld_2_p4, reg8_ld_5_p4, reg16m_inc_ld_2_p4, rsff_2_p4,
       rsff_3_p4, rsff_4_p4, rsff_6_p4, rsff_7_p4, rsff_8_p4, rsff_9_p4;
  wire [3:0] IR27__24;
  wire [6:0] PSW15__8;
  wire [7:0] IR7__0, IR15__8, IR23__16, outDW7__0, outDW15__8, reg8_ld_2_p3, reg8_ld_5_p3;
  wire [7:4] IR31__24;
  wire [7:5] PSW7__0;
  wire [15:0] GPR15__0, mp2_16b_2_p3, outADDPC, outSP;

  // REG8_LD reg8_ld_1: pin names not known; wires that end beside it: CLK, MDR_2, IR23__16, CREGBUS[6]
  // REG8_LD reg8_ld_2: pin names not known; wires that end beside it: CLK, MDR_2, reg8_ld_2_p3, reg8_ld_2_p4
  and and_1 (reg8_ld_2_p4, CREGBUS[12], ~outCNTB);  // AND_Gate
  // REG1_CL_INC reg1_cl_inc_1: pin names not known; wires that end beside it: CREGBUS[11], CLK, outCNTB, CREGBUS[10]
  // MP8_16b mp8_16b_1: pin names not known; wires that end beside it: CMEMBUS[10], CMEMBUS[6], CMEMBUS[5], PC_2, {IR15__8, IR7__0}, GPR15__0, out_21, mp8_16b_1_p8, outSP, IVTPPDSP, 1'b1
  // REG16m_INC_LD reg16m_inc_ld_1: pin names not known; wires that end beside it: CLK, mp8_16b_1_p8, MAR_2, CMEMBUS[0], CMEMBUS[1], CMEMBUS[1]
  // DC4_16 dc4_16_1: pin names not known; wires that end beside it: IR31__24, PSW[0], bezadrinst, branchinst, jmpinst, adrinst
  // DC4_16 dc4_16_2: pin names not known; wires that end beside it: IR27__24, jmpinst, INSTRUCBUS[13], INSTRUCBUS[14]
  and and_2 (ADDRBUS[0], ~IR23__16[0], ~IR23__16[1], ~IR23__16[2], ~IR23__16[3], ~IR23__16[4], ~IR23__16[5], ~IR23__16[6], ~IR23__16[7], adrinst);  // AND_Gate
  and and_3 (ADDRBUS[3], IR23__16[4], IR23__16[5], ~IR23__16[6], ~IR23__16[7], adrinst);  // AND_Gate
  and and_4 (ADDRBUS[6], ~IR23__16[4], IR23__16[5], IR23__16[6], ~IR23__16[7], adrinst);  // AND_Gate
  // REG8_LD reg8_ld_3: pin names not known; wires that end beside it: CLK, MDR_2, {IR31__24, IR27__24}, CREGBUS[7]
  // REG8_LD reg8_ld_4: pin names not known; wires that end beside it: CLK, MDR_2, IR15__8, CREGBUS[5]
  // REG8_LD reg8_ld_5: pin names not known; wires that end beside it: CLK, MDR_2, reg8_ld_5_p3, reg8_ld_5_p4
  and and_5 (reg8_ld_5_p4, CREGBUS[13], outCNTB);
  // MP4_16b mp4_16b_1: pin names not known; wires that end beside it: CREGBUS[9], CREGBUS[8], {reg8_ld_2_p3, reg8_ld_5_p3}, {IR15__8, IR7__0}, mp4_16b_1_p5, mp4_16b_1_p5, GPR15__0, 1'b1
  // REG16 reg16_1: pin names not known; wires that end beside it: CLK, out_21, CREGBUS[0], CREGBUS[1], CREGBUS[2]
  // MP8_8b mp8_8b_1: pin names not known; wires that end beside it: CMEMBUS[9], CMEMBUS[8], CMEMBUS[7], DIN, Akumulator[15:8], Akumulator[7:0], PC_2[15:8], mp8_8b_1_p8, PC_2[7:0], {PSW7__0, PSW[4:0]}, {PSW[15], PSW15__8}, 1'b1
  // REG8_LD reg8_ld_6: pin names not known; wires that end beside it: CLK, mp8_8b_1_p8, MDR_2, CMEMBUS[2]
  // DC4_16 dc4_16_3: pin names not known; wires that end beside it: IR27__24, bezadrinst, INSTRUCBUS[0], INSTRUCBUS[1], INSTRUCBUS[2], INSTRUCBUS[3], INSTRUCBUS[4], INSTRUCBUS[5], INSTRUCBUS[6], INSTRUCBUS[7]
  // DC4_16 dc4_16_4: pin names not known; wires that end beside it: IR27__24, adrinst, INSTRUCBUS[15], INSTRUCBUS[16], INSTRUCBUS[17], INSTRUCBUS[18], INSTRUCBUS[19], INSTRUCBUS[20]
  // REG8_LD reg8_ld_7: pin names not known; wires that end beside it: CLK, MDR_2, IR7__0, CREGBUS[4]
  and and_6 (ADDRBUS[1], ~IR23__16[0], ~IR23__16[1], ~IR23__16[2], ~IR23__16[3], IR23__16[4], ~IR23__16[5], ~IR23__16[6], ~IR23__16[7], adrinst);  // AND_Gate
  and and_7 (ADDRBUS[4], ~IR23__16[4], ~IR23__16[5], IR23__16[6], ~IR23__16[7], adrinst);  // AND_Gate
  // REG8_LD reg8_ld_8: pin names not known; wires that end beside it: CLK, MDR_2, outDW15__8, CREGBUS[14]
  not not_1 (not_1_out, RST);
  // RSFF rsff_1: pin names not known; wires that end beside it: CFFBUS[1], CLK, CFFBUS[0], not_1_out, PHASEFFBUS[0]
  // MP4_16b mp4_16b_2: pin names not known; wires that end beside it: CMEMBUS[12], CMEMBUS[11], {IR23__16, IR15__8}, outADDPC, mp4_16b_2_p5, {outDW15__8, outDW7__0}, 1'b1
  // MP2_16b mp2_16b_1: pin names not known; wires that end beside it: RST, mp4_16b_2_p5, mp2_16b_1_p3, 16'h1000, 1'b1
  // REG16m_INC_LD reg16m_inc_ld_2: pin names not known; wires that end beside it: CLK, mp2_16b_1_p3, PC_2, reg16m_inc_ld_2_p4, CMEMBUS[4], CMEMBUS[4]
  // DC4_16 dc4_16_5: pin names not known; wires that end beside it: IR27__24, branchinst, INSTRUCBUS[8], INSTRUCBUS[9], INSTRUCBUS[10], INSTRUCBUS[11], INSTRUCBUS[12]
  or or_1 (reg16m_inc_ld_2_p4, CMEMBUS[3], RST);
  and and_8 (ADDRBUS[2], ~IR23__16[0], ~IR23__16[1], ~IR23__16[2], ~IR23__16[3], ~IR23__16[4], IR23__16[5], ~IR23__16[6], ~IR23__16[7], adrinst);  // AND_Gate
  and and_9 (ADDRBUS[5], IR23__16[4], ~IR23__16[5], IR23__16[6], ~IR23__16[7], adrinst);  // AND_Gate
  // REG8_LD reg8_ld_9: pin names not known; wires that end beside it: CLK, MDR_2, outDW7__0, CREGBUS[15]
  // RSFF rsff_2: pin names not known; wires that end beside it: CFFBUS[3], CLK, CFFBUS[2], rsff_2_p4, PHASEFFBUS[1]
  not not_2 (rsff_2_p4, RST);
  not not_3 (not_3_out, RST);
  or or_2 (or_2_out, INSTRUCBUS[2], INSTRUCBUS[6]);
  or or_3 (or_3_out, INSTRUCBUS[2], INSTRUCBUS[6]);
  and and_10 (and_10_out, Akumulator[15], out_21[15], ~Sabirac[15]);  // AND_Gate
  and and_11 (and_11_out, ~Akumulator[15], ~out_21[15], Sabirac[15]);  // AND_Gate
  and and_12 (and_12_out, Akumulator[15], ~Oduzimac[15]);  // AND_Gate
  and and_13 (and_13_out, ~Akumulator[15], Oduzimac[15]);  // AND_Gate
  or or_4 (or_4_out, INSTRUCBUS[2], INSTRUCBUS[6]);
  // REG16 reg16_2: pin names not known; wires that end beside it: CLK, 16'hf000, outSP, RST, CMEMBUS[13], CMEMBUS[14]
  // REG16_LD reg16_ld_1: pin names not known; wires that end beside it: CLK, not_3_out, Akumulator, out_26, CREGBUS[16]
  or or_5 (or_5_out, INSTRUCBUS[2], INSTRUCBUS[6]);
  and and_14 (and_14_out, or_2_out, MDR_2[1]);
  and and_15 (and_15_out, ~Akumulator[0], ~Akumulator[1], ~Akumulator[2], ~Akumulator[3], ~Akumulator[4], ~Akumulator[5], ~Akumulator[6], ~Akumulator[7]);  // AND_Gate
  and and_16 (and_16_out, ~Akumulator[8], ~Akumulator[9], ~Akumulator[10], ~Akumulator[11], ~Akumulator[12], ~Akumulator[13], ~Akumulator[14], ~Akumulator[15]);  // AND_Gate
  or or_6 (or_6_out, INSTRUCBUS[2], INSTRUCBUS[6]);
  and and_17 (and_17_out, or_3_out, MDR_2[3]);
  or or_7 (or_7_out, and_10_out, and_11_out);
  or or_8 (or_8_out, and_12_out, and_13_out);
  and and_18 (and_18_out, or_4_out, MDR_2[4]);
  and and_19 (and_19_out, INSTRUCBUS[17], Signali[2]);
  and and_20 (and_20_out, INSTRUCBUS[18], Signali[3]);
  and and_21 (and_21_out, INSTRUCBUS[3], Signali[0]);
  and and_22 (and_22_out, INSTRUCBUS[4], Signali[1]);
  or or_9 (or_9_out, INSTRUCBUS[2], INSTRUCBUS[6]);
  // RSFF rsff_3: pin names not known; wires that end beside it: CFFBUS[5], CLK, CFFBUS[4], rsff_3_p4, PHASEFFBUS[2]
  not not_4 (rsff_3_p4, RST);
  and and_23 (and_23_out, and_15_out, and_16_out);
  and and_24 (and_24_out, or_6_out, MDR_2[2]);
  and and_25 (and_25_out, adresneinstr, Akumulator[15]);
  and and_26 (and_26_out, INSTRUCBUS[17], or_7_out);
  and and_27 (and_27_out, INSTRUCBUS[18], or_8_out);
  or or_10 (or_10_out, and_19_out, and_20_out, and_21_out, and_22_out);
  and and_28 (and_28_out, or_9_out, MDR_2[7]);
  // MP2_16b mp2_16b_2: pin names not known; wires that end beside it: CREGBUS[17], out_21, mp2_16b_2_p3, Akumulator, 1'b1
  GPR16x16 gpr16x16_1 (.DI15__0(mp2_16b_2_p3), .A3__0(IR23__16[3:0]), .WR(CREGBUS[3]), .CLK(CLK), .DO15__0(GPR15__0));
  and and_29 (and_29_out, ~MDR_2[0], or_5_out, CPSW[1]);  // AND_Gate
  and and_30 (and_30_out, MDR_2[0], or_5_out, CPSW[1]);
  or or_11 (or_11_out, and_14_out, and_31_out);
  and and_31 (and_31_out, adresneinstr, and_23_out);
  or or_12 (or_12_out, and_24_out, and_25_out);
  or or_13 (or_13_out, and_26_out, and_27_out);
  or or_14 (or_14_out, and_18_out, or_10_out);
  or or_15 (or_15_out, and_29_out, CPSW[0]);
  and and_32 (and_32_out, ~or_12_out, CPSW[2]);  // AND_Gate
  and and_33 (and_33_out, CPSW[2], or_12_out);
  or or_16 (or_16_out, and_17_out, or_13_out);
  and and_34 (and_34_out, ~or_16_out, CPSW[5]);  // AND_Gate
  and and_35 (and_35_out, CPSW[5], or_16_out);
  and and_36 (and_36_out, ~or_14_out, CPSW[4]);  // AND_Gate
  and and_37 (and_37_out, CPSW[4], or_14_out);
  and and_38 (and_38_out, ~and_28_out, CPSW[6]);  // AND_Gate
  and and_39 (and_39_out, CPSW[6], and_28_out);
  // ADD16 add16_1: pin names not known; wires that end beside it: {{9{IR23__16[7]}}, IR23__16[6:0]}, outADDPC, PC_2
  // RSFF rsff_4: pin names not known; wires that end beside it: CFFBUS[7], CLK, CFFBUS[6], rsff_4_p4, PHASEFFBUS[3]
  not not_5 (rsff_4_p4, RST);
  not not_6 (not_6_out, RST);
  // RSFF rsff_5: pin names not known; wires that end beside it: or_15_out, CLK, and_30_out, not_6_out, PSW[0]
  and and_40 (and_40_out, ~or_11_out, CPSW[3]);  // AND_Gate
  and and_41 (and_41_out, CPSW[3], or_11_out);
  // RSFF rsff_6: pin names not known; wires that end beside it: and_40_out, CLK, and_41_out, rsff_6_p4, PSW[1]
  not not_7 (rsff_6_p4, RST);
  // RSFF rsff_7: pin names not known; wires that end beside it: and_32_out, CLK, and_33_out, rsff_7_p4, PSW[2]
  not not_8 (rsff_7_p4, RST);
  // RSFF rsff_8: pin names not known; wires that end beside it: and_34_out, CLK, and_35_out, rsff_8_p4, PSW[3]
  not not_9 (rsff_8_p4, RST);
  // RSFF rsff_9: pin names not known; wires that end beside it: and_36_out, CLK, and_37_out, rsff_9_p4, PSW[4]
  not not_10 (rsff_9_p4, RST);
  not not_11 (not_11_out, RST);
  // RSFF rsff_10: pin names not known; wires that end beside it: and_38_out, CLK, and_39_out, not_11_out, PSW[15]
  or or_17 (adresneinstr, INSTRUCBUS[15], INSTRUCBUS[17], INSTRUCBUS[19], INSTRUCBUS[18], INSTRUCBUS[3], INSTRUCBUS[4], INSTRUCBUS[20]);

  // Other names for the same wires on the sheet: A7__0[7:0] = A; immed = ADDRBUS[0]; memdir = ADDRBUS[1];
  //   memind = ADDRBUS[2]; regind = ADDRBUS[3]; preincr = ADDRBUS[4]; postdec = ADDRBUS[5]; regdir = ADDRBUS[6];
  //   ALU7__0[7:0] = ALU; B7__0[7:0] = B; stFETCH = CFFBUS[0]; clFETCH = CFFBUS[1]; stADDR = CFFBUS[2];
  //   clADDR = CFFBUS[3]; stEXEC = CFFBUS[4]; clEXEC = CFFBUS[5]; stINTR = CFFBUS[6]; clINTR = CFFBUS[7];
  //   ldMAR = CMEMBUS[0]; incMAR = CMEMBUS[1]; ldMDR = CMEMBUS[2]; ldPC = CMEMBUS[3]; incPC = CMEMBUS[4];
  //   mxMAR0 = CMEMBUS[5]; mxMAR1 = CMEMBUS[6]; mxMDR0 = CMEMBUS[7]; mxMDR1 = CMEMBUS[8]; mxMDR2 = CMEMBUS[9];
  //   mxMAR2 = CMEMBUS[10]; mxPC0 = CMEMBUS[11]; mxPC1 = CMEMBUS[12]; incSP = CMEMBUS[13]; decSP = CMEMBUS[14];
  //   clPSWSTART = CPSW[0]; stPSWSTART = CPSW[1]; ldN = CPSW[2]; ldZ = CPSW[3]; ldC = CPSW[4]; ldV = CPSW[5];
  //   ldI = CPSW[6]; ldB = CREGBUS[0]; incB = CREGBUS[1]; decB = CREGBUS[2]; wrGPR = CREGBUS[3];
  //   ldIR7__0 = CREGBUS[4]; ldIR15__8 = CREGBUS[5]; ldIR23__16 = CREGBUS[6]; ldIR31__24 = CREGBUS[7];
  //   mxB0 = CREGBUS[8]; mxB1 = CREGBUS[9]; incCNTB = CREGBUS[10]; clCNTB = CREGBUS[11]; ldB15__8 = CREGBUS[12];
  //   ldB7__0 = CREGBUS[13]; ldDW15__8 = CREGBUS[14]; ldDW7__0 = CREGBUS[15]; ldIVTP = CREGBUS[16];
  //   mxGPR0 = CREGBUS[17]; Din7__0[7:0] = DIN; inMAR[15:0] = MAR; inMDR[7:0] = MDR; inPC[15:0] = PC;
  //   HALT = INSTRUCBUS[0]; RTS = INSTRUCBUS[1]; RTI = INSTRUCBUS[2]; ROR = INSTRUCBUS[3]; RORC = INSTRUCBUS[4];
  //   PUSHPSW = INSTRUCBUS[5]; POPPSW = INSTRUCBUS[6]; STIVTP = INSTRUCBUS[7]; BGREU = INSTRUCBUS[8];
  //   BLSSU = INSTRUCBUS[9]; BLEQU = INSTRUCBUS[10]; JGRT = INSTRUCBUS[11]; JLEQ = INSTRUCBUS[12];
  //   JMP = INSTRUCBUS[13]; JSR = INSTRUCBUS[14]; LD = INSTRUCBUS[15]; ST = INSTRUCBUS[16]; ADD = INSTRUCBUS[17];
  //   DEC = INSTRUCBUS[18]; OR = INSTRUCBUS[19]; STRFIND = INSTRUCBUS[20]; IR31__24[3:0] = IR27__24;
  //   outA[15:0] = Akumulator; A15 = Akumulator[15]; outADDACC[15:0] = Sabirac; ADDACC15 = Sabirac[15];
  //   outB[15:0] = out_21; B15 = out_21[15]; outDECACC[15:0] = Oduzimac; DECACC15 = Oduzimac[15];
  //   outIVTP[15:0] = out_26; outIVTPADD[15:0] = IVTPPDSP; outMAR[15:0] = MAR_2; MDR0 = MDR_2[0]; outMDR[7:0] = MDR_2;
  //   MDR1 = MDR_2[1]; MDR2 = MDR_2[2]; MDR3 = MDR_2[3]; MDR4 = MDR_2[4]; MDR15 = MDR_2[7]; outPC[15:0] = PC_2;
  //   FETCH = PHASEFFBUS[0]; ADDR = PHASEFFBUS[1]; EXEC = PHASEFFBUS[2]; INTR = PHASEFFBUS[3];
  //   PSW7__0[4:0] = PSW[4:0]; PSWSTART = PSW[0]; PSWZ = PSW[1]; PSWN = PSW[2]; PSWV = PSW[3]; PSWC = PSW[4];
  //   PSW15__8[7] = PSW[15]; PSWI = PSW[15]; carryROR = Signali[0]; carryRORC = Signali[1]; checkADDC = Signali[2];
  //   checkDECC = Signali[3]

  // Notes on the sheet:
  //   Registar B
  //   Instrukcijski registar
  //   Prepoznavanje nacina adresiranja
  //   Pomocni registri
  //   MAR
  //   Dekoderi za prepoznavanje instrukcije na osnovu sadrzaja registra IR31..24
  //   MDR
  //   PC
  //   FF za pokretanje FETCH, ADDR, EXEC i INTR faze izvršavanja instrukcije
  //   Registarski fajl
  //   SP
  //   IVTP
  //   Programska statusna reč (PSW)
  //   Sabirac PC + pomeraj
endmodule

module FETCH (
  input  in_1,
  input  in_2,
  input  in_3,
  input  [3:0] PHASEFFBUS,
  input  [20:0] INSTRUCBUS,
  input  [6:0] ADDRBUS,
  input  [15:0] PSW,
  output [14:0] CMEMBUS,
  output [7:0] CFFBUS,
  output [17:0] CREGBUS,
  output rdMEM
);

  wire addr, adr2, adr4, and_3_out, and_4_out, and_5_out, and_6_out, and_7_out, and_8_out, and_9_out,
       and_10_out, and_11_out, and_12_out, and_13_out, and_14_out, badMode, badOC, bezadr1, bradr2, branch2,
       brbezadr1, brbranch2, brcnd, brgrinst, brjmp3, brnotFCBUS, bruncnd, clBYTE2, clFETCH,
       demux1_2_1_out_3, grinst, incBYTE2, incPC, jmp3, ldIR7__0, ldIR15__8, ldIR23__16, ldIR31__24, ldMAR,
       ldMDR, not_1_out, not_3_out, not_4_out, not_5_out, notPSWSTandFETCH, or_5_out, or_6_out, or_8_out,
       outBYTE2, rdMEM_t, reg8_inc_ld_1_p5, reg8_inc_ld_1_p6, stADDR, stEXEC;
  wire [3:0] dc4_16_1_p1;
  wire [4:0] reg8_inc_ld_1_p3;
  wire [7:0] reg8_inc_ld_1_p4;
  wire [23:22] rom256x24_1_dout;

  // REG1_CL_INC reg1_cl_inc_1: pin names not known; wires that end beside it: clBYTE2, in_2, outBYTE2, incBYTE2
  not not_1 (not_1_out, in_1);
  // REG8_INC_LD reg8_inc_ld_1: pin names not known; wires that end beside it: in_2, not_1_out, {3'b000, reg8_inc_ld_1_p3}, reg8_inc_ld_1_p4, reg8_inc_ld_1_p5, reg8_inc_ld_1_p6
  // DC4_16 dc4_16_1: pin names not known; wires that end beside it: dc4_16_1_p1, 1'b1, bruncnd, notPSWSTandFETCH, brbezadr1, brbranch2, bradr2, brjmp3, brnotFCBUS, brgrinst
  or or_1 (bezadr1, INSTRUCBUS[0], INSTRUCBUS[1], INSTRUCBUS[2], INSTRUCBUS[3], INSTRUCBUS[4], INSTRUCBUS[5], INSTRUCBUS[6], INSTRUCBUS[7]);
  or or_2 (branch2, INSTRUCBUS[8], INSTRUCBUS[9], INSTRUCBUS[10]);
  or or_3 (jmp3, INSTRUCBUS[11], INSTRUCBUS[12], INSTRUCBUS[13], INSTRUCBUS[14]);
  not not_2 (reg8_inc_ld_1_p6, reg8_inc_ld_1_p5);
  ROM256x24 rom256x24_1 (
    .A7__0(reg8_inc_ld_1_p4), .CS(1'b1),
    .DOUT({rom256x24_1_dout, reg8_inc_ld_1_p3, dc4_16_1_p1, stEXEC, stADDR, clFETCH, ldIR7__0, ldIR15__8, incBYTE2, ldIR23__16, ldIR31__24, ldMDR, rdMEM_t, clBYTE2, incPC, ldMAR}));
  or or_4 (reg8_inc_ld_1_p5, bruncnd, brcnd);
  or or_5 (or_5_out, ADDRBUS[3], ADDRBUS[4], ADDRBUS[5], ADDRBUS[6]);
  or or_6 (or_6_out, ADDRBUS[0], ADDRBUS[1], ADDRBUS[2]);
  or or_7 (addr, INSTRUCBUS[15], INSTRUCBUS[16], INSTRUCBUS[17], INSTRUCBUS[18], INSTRUCBUS[19], INSTRUCBUS[20]);
  and and_1 (adr2, addr, or_5_out);
  and and_2 (adr4, addr, or_6_out);
  not not_3 (not_3_out, PHASEFFBUS[0]);
  not not_4 (not_4_out, PSW[0]);
  or or_8 (or_8_out, not_3_out, not_4_out);
  not not_5 (not_5_out, in_3);
  and and_3 (and_3_out, or_8_out, notPSWSTandFETCH);
  and and_4 (and_4_out, brbezadr1, bezadr1);
  and and_5 (and_5_out, brbranch2, branch2);
  and and_6 (and_6_out, bradr2, adr2);
  and and_7 (and_7_out, brjmp3, jmp3);
  and and_8 (and_8_out, brnotFCBUS, not_5_out);
  and and_9 (and_9_out, brgrinst, grinst);
  and and_10 (and_10_out, ~INSTRUCBUS[0], ~INSTRUCBUS[1], ~INSTRUCBUS[2], ~INSTRUCBUS[3], ~INSTRUCBUS[4], ~INSTRUCBUS[5], ~INSTRUCBUS[6], ~INSTRUCBUS[7], ~INSTRUCBUS[8], ~INSTRUCBUS[9], ~INSTRUCBUS[10], ~INSTRUCBUS[11], ~INSTRUCBUS[12], ~INSTRUCBUS[13], ~INSTRUCBUS[14], ~INSTRUCBUS[15], ~INSTRUCBUS[16], ~INSTRUCBUS[17], ~INSTRUCBUS[18], ~INSTRUCBUS[19], ~INSTRUCBUS[20]);  // AND_Gate
  DEMUX1_2 demux1_2_1 (.out_3(demux1_2_1_out_3), .in_1(and_10_out), .out_4(badOC), .in_2(1'b1));
  or or_9 (grinst, badOC, badMode);
  or or_10 (brcnd, and_3_out, and_4_out, and_5_out, and_6_out, and_7_out, and_8_out, and_9_out);
  and and_11 (and_11_out, demux1_2_1_out_3, outBYTE2);
  and and_12 (and_12_out, ~ADDRBUS[0], ~ADDRBUS[1], ~ADDRBUS[2], ~ADDRBUS[3], ~ADDRBUS[4], ~ADDRBUS[5], ~ADDRBUS[6], addr);  // AND_Gate
  and and_13 (and_13_out, INSTRUCBUS[16], ADDRBUS[0], outBYTE2);
  and and_14 (and_14_out, and_11_out, and_12_out);
  or or_11 (badMode, and_14_out, and_13_out);
  assign CMEMBUS[0] = ldMAR ? 1'b1 : 1'bz;  // Controlled_Buffer controlled_buffer_1
  assign CMEMBUS[2] = ldMDR ? 1'b1 : 1'bz;  // Controlled_Buffer controlled_buffer_2
  assign CMEMBUS[4] = incPC ? 1'b1 : 1'bz;  // Controlled_Buffer controlled_buffer_3
  assign CFFBUS[1] = clFETCH ? 1'b1 : 1'bz;  // Controlled_Buffer controlled_buffer_4
  assign CFFBUS[2] = stADDR ? 1'b1 : 1'bz;  // Controlled_Buffer controlled_buffer_5
  assign CFFBUS[4] = stEXEC ? 1'b1 : 1'bz;  // Controlled_Buffer controlled_buffer_6
  assign CREGBUS[4] = ldIR7__0 ? 1'b1 : 1'bz;  // Controlled_Buffer controlled_buffer_7
  assign CREGBUS[5] = ldIR15__8 ? 1'b1 : 1'bz;  // Controlled_Buffer controlled_buffer_8
  assign CREGBUS[6] = ldIR23__16 ? 1'b1 : 1'bz;  // Controlled_Buffer controlled_buffer_9
  assign CREGBUS[7] = ldIR31__24 ? 1'b1 : 1'bz;  // Controlled_Buffer controlled_buffer_10
  assign rdMEM = rdMEM_t ? 1'b1 : 1'bz;  // Controlled_Buffer controlled_buffer_11

  // Other names for the same wires on the sheet: immed = ADDRBUS[0]; memdir = ADDRBUS[1]; memind = ADDRBUS[2];
  //   regind = ADDRBUS[3]; preincr = ADDRBUS[4]; postdec = ADDRBUS[5]; regdir = ADDRBUS[6]; CLK = in_2; FCBUS = in_3;
  //   HALT = INSTRUCBUS[0]; RTS = INSTRUCBUS[1]; RTI = INSTRUCBUS[2]; ROR = INSTRUCBUS[3]; RORC = INSTRUCBUS[4];
  //   PUSHPSW = INSTRUCBUS[5]; POPPSW = INSTRUCBUS[6]; STIVTP = INSTRUCBUS[7]; BGREU = INSTRUCBUS[8];
  //   BLSSU = INSTRUCBUS[9]; BLEQU = INSTRUCBUS[10]; JGRT = INSTRUCBUS[11]; JLEQ = INSTRUCBUS[12];
  //   JMP = INSTRUCBUS[13]; JSR = INSTRUCBUS[14]; LD = INSTRUCBUS[15]; ST = INSTRUCBUS[16]; ADD = INSTRUCBUS[17];
  //   DEC = INSTRUCBUS[18]; OR = INSTRUCBUS[19]; STRFIND = INSTRUCBUS[20]; FETCH = PHASEFFBUS[0]; PSWSTART = PSW[0];
  //   rst = in_1

  // Notes on the sheet:
  //   Operaciona jedinica
  //   Kontrolna jedinica
endmodule

module ADDR (
  input  in_1,
  input  in_2,
  input  in_3,
  input  [3:0] PHASEFFBUS,
  input  [20:0] INSTRUCBUS,
  input  [6:0] ADDRBUS,
  output [14:0] CMEMBUS,
  output [7:0] CFFBUS,
  output [17:0] CREGBUS,
  output rdMEM
);

  wire and_1_out, and_2_out, and_3_out, bradr, brcnd, brnotADDR, brnotFCBUS, brSTORE, bruncnd, clADDR,
       clCNTB, decB, incB, incCNTB, incMAR, ldB, ldB7__0, ldB15__8, ldMAR, ldMDR, mp2_8b_1_p3, mxB0, mxB1,
       mxMAR0, mxMAR1, not_1_out, not_3_out, not_4_out, rdMEM_t, reg8_inc_ld_1_p5, reg8_inc_ld_1_p6, stEXEC,
       wrGPR;
  wire [2:0] dc3_8_1_p1;
  wire [4:0] mp2_8b_1_p2;
  wire [7:0] kmadr_1_adr6__0, reg8_inc_ld_1_p4;

  not not_1 (not_1_out, in_1);
  KMADR kmadr_1 (
    .immed(ADDRBUS[0]), .memdir(ADDRBUS[1]), .memind(ADDRBUS[2]), .regind(ADDRBUS[3]), .preincr(ADDRBUS[4]),
    .postdec(ADDRBUS[5]), .regdir(ADDRBUS[6]), .Adr6__0(kmadr_1_adr6__0));
  // MP2_8b mp2_8b_1: pin names not known; wires that end beside it: bradr, {3'b000, mp2_8b_1_p2}, mp2_8b_1_p3, kmadr_1_adr6__0
  // REG8_INC_LD reg8_inc_ld_1: pin names not known; wires that end beside it: in_2, not_1_out, mp2_8b_1_p3, reg8_inc_ld_1_p4, reg8_inc_ld_1_p5, reg8_inc_ld_1_p6
  // DC3_8 dc3_8_1: pin names not known; wires that end beside it: dc3_8_1_p1, 1'b1, bruncnd, brnotADDR, brSTORE, brnotFCBUS, bradr
  not not_2 (reg8_inc_ld_1_p6, reg8_inc_ld_1_p5);
  ROM256x26 rom256x26_1 (
    .A7__0(reg8_inc_ld_1_p4), .CS(1'b1),
    .DOUT({mp2_8b_1_p2, dc3_8_1_p1, stEXEC, clADDR, decB, wrGPR, incB, mxB1, mxMAR1, ldB7__0, incCNTB, incMAR, ldB15__8, ldMDR, rdMEM_t, clCNTB, mxMAR0, ldMAR, mxB0, ldB}));
  or or_1 (reg8_inc_ld_1_p5, bruncnd, brcnd, bradr);
  not not_3 (not_3_out, PHASEFFBUS[1]);
  not not_4 (not_4_out, in_3);
  and and_1 (and_1_out, not_3_out, brnotADDR);
  and and_2 (and_2_out, INSTRUCBUS[16], brSTORE);
  and and_3 (and_3_out, brnotFCBUS, not_4_out);
  or or_2 (brcnd, and_1_out, and_2_out, and_3_out);
  assign CMEMBUS[0] = ldMAR ? 1'b1 : 1'bz;  // Controlled_Buffer controlled_buffer_1
  assign CMEMBUS[1] = incMAR ? 1'b1 : 1'bz;  // Controlled_Buffer controlled_buffer_2
  assign CMEMBUS[2] = ldMDR ? 1'b1 : 1'bz;  // Controlled_Buffer controlled_buffer_3
  assign CMEMBUS[5] = mxMAR0 ? 1'b1 : 1'bz;  // Controlled_Buffer controlled_buffer_4
  assign CMEMBUS[6] = mxMAR1 ? 1'b1 : 1'bz;  // Controlled_Buffer controlled_buffer_5
  assign CREGBUS[0] = ldB ? 1'b1 : 1'bz;  // Controlled_Buffer controlled_buffer_6
  assign CREGBUS[1] = incB ? 1'b1 : 1'bz;  // Controlled_Buffer controlled_buffer_7
  assign CREGBUS[2] = decB ? 1'b1 : 1'bz;  // Controlled_Buffer controlled_buffer_8
  assign CREGBUS[3] = wrGPR ? 1'b1 : 1'bz;  // Controlled_Buffer controlled_buffer_9
  assign CREGBUS[8] = mxB0 ? 1'b1 : 1'bz;  // Controlled_Buffer controlled_buffer_10
  assign CREGBUS[9] = mxB1 ? 1'b1 : 1'bz;  // Controlled_Buffer controlled_buffer_11
  assign CREGBUS[10] = incCNTB ? 1'b1 : 1'bz;  // Controlled_Buffer controlled_buffer_12
  assign CREGBUS[11] = clCNTB ? 1'b1 : 1'bz;  // Controlled_Buffer controlled_buffer_13
  assign CREGBUS[12] = ldB15__8 ? 1'b1 : 1'bz;  // Controlled_Buffer controlled_buffer_14
  assign CREGBUS[13] = ldB7__0 ? 1'b1 : 1'bz;  // Controlled_Buffer controlled_buffer_15
  assign CFFBUS[3] = clADDR ? 1'b1 : 1'bz;  // Controlled_Buffer controlled_buffer_16
  assign CFFBUS[4] = stEXEC ? 1'b1 : 1'bz;  // Controlled_Buffer controlled_buffer_17
  assign rdMEM = rdMEM_t ? 1'b1 : 1'bz;  // Controlled_Buffer controlled_buffer_18

  // Other names for the same wires on the sheet: immed = ADDRBUS[0]; memdir = ADDRBUS[1]; memind = ADDRBUS[2];
  //   regind = ADDRBUS[3]; preincr = ADDRBUS[4]; postdec = ADDRBUS[5]; regdir = ADDRBUS[6]; CLK = in_2; FCBUS = in_3;
  //   ST = INSTRUCBUS[16]; ADDR = PHASEFFBUS[1]; rst = in_1

  // Notes on the sheet:
  //   Operaciona jedinica
  //   Upravljacka jedinica
endmodule

module EXEC (
  input  in_1,
  input  in_2,
  input  in_3,
  input  [7:0] B,
  input  [15:0] in_5,
  input  [7:0] in_6,
  input  [3:0] PHASEFFBUS,
  input  [20:0] INSTRUCBUS,
  input  [6:0] ADDRBUS,
  input  [15:0] PSW,
  output [7:0] A,
  output [7:0] ALU,
  output [15:0] Akumulator,
  output [15:0] Sabirac,
  output [15:0] Oduzimac,
  output [3:0] Signali,
  output [14:0] CMEMBUS,
  output [7:0] CFFBUS,
  output [6:0] CPSW,
  output [17:0] CREGBUS,
  output rdMEM,
  output wrMEM
);

  wire ACCEQMDR, and_1_out, and_2_out, and_3_out, and_4_out, and_5_out, and_6_out, and_7_out, and_8_out,
       and_9_out, and_10_out, and_11_out, and_12_out, brcnd, brinsttype, brnotACCEQMDR, brnotbrinsttype,
       brnotbrorjmp, brnotENDOFARRAY, brnotEXEC, brnotFCBUS, bropr, brorjmp, brregdir, bruncnd, clEXEC,
       clPSWSTART, clSTRCNT, decSP, ENDOFARRAY, incMAR, incSP, incSTRCNT, ldA, ldC, ldDW7__0, ldDW15__8, ldI,
       ldIVTP, ldMAR, ldMDR, ldN, ldPC, ldV, ldZ, mp8_16b_1_p8, mxA0, mxA1, mxA2, mxGPR0, mxMAR0, mxMAR1,
       mxMAR2, mxMDR0, mxMDR1, mxMDR2, mxPC0, mxPC1, not_1_out, not_2_out, not_3_out, not_4_out, not_5_out,
       not_6_out, not_7_out, not_8_out, not_9_out, or_1_out, or_2_out, or_3_out, rdMEM_t, stINTR, stPSWSTART,
       wrGPR, wrMEM_t, xor_1_out;
  wire [3:0] dc4_16_1_p1;
  wire [5:0] kmopr_1_adr5__0, mp2_6b_1_p3, reg6_inc_ld_1_a5__0, rom64x46_1_dout45__32;
  wire [15:0] outOR, outROR, outRORC, outSTRCNT;

  // DC4_16 dc4_16_1: pin names not known; wires that end beside it: dc4_16_1_p1, 1'b1, bruncnd, brnotEXEC, brregdir, brnotFCBUS, brnotbrorjmp, brnotbrinsttype, brnotENDOFARRAY, brnotACCEQMDR, bropr
  not not_1 (not_1_out, in_1);
  // REG16 reg16_1: pin names not known; wires that end beside it: clSTRCNT, in_2, outSTRCNT, incSTRCNT
  // MP8_16b mp8_16b_1: pin names not known; wires that end beside it: mxA2, mxA1, mxA0, in_5, Sabirac, Oduzimac, outROR, mp8_16b_1_p8, outRORC, outOR, {16{1'b1}}, outSTRCNT, 1'b1
  // REG16_LD reg16_ld_1: pin names not known; wires that end beside it: in_2, not_1_out, mp8_16b_1_p8, Akumulator, ldA
  OR16b or16b_1 (.DOUT(outOR), .A15__0(Akumulator), .B15__0(in_5));
  KMOPR kmopr_1 (
    .LD(INSTRUCBUS[15]), .ST(INSTRUCBUS[16]), .Adr5__0(kmopr_1_adr5__0), .ADD(INSTRUCBUS[17]),
    .OR(INSTRUCBUS[19]), .DEC(INSTRUCBUS[18]), .BGREU(INSTRUCBUS[8]), .BLSSU(INSTRUCBUS[9]),
    .BLEQU(INSTRUCBUS[10]), .JGRT(INSTRUCBUS[11]), .JMP(INSTRUCBUS[13]), .JSR(INSTRUCBUS[14]),
    .POPPSW(INSTRUCBUS[6]), .RTI(INSTRUCBUS[2]), .RTS(INSTRUCBUS[1]), .PUSHPSW(INSTRUCBUS[5]),
    .RORC(INSTRUCBUS[4]), .ROR(INSTRUCBUS[3]), .STIVTP(INSTRUCBUS[7]), .STRFIND(INSTRUCBUS[20]),
    .HALT(INSTRUCBUS[0]), .JLEQ(INSTRUCBUS[12]));
  not not_2 (not_2_out, in_1);
  REG6_INC_LD reg6_inc_ld_1 (
    .I5__0(mp2_6b_1_p3), .LD(or_1_out), .INC(not_3_out), .mr(not_2_out), .CLK(in_2),
    .A5__0(reg6_inc_ld_1_a5__0));
  not not_3 (not_3_out, or_1_out);
  ROM64x46 rom64x46_1 (
    .A5__0(reg6_inc_ld_1_a5__0), .CS(1'b1),
    .DOUT45__32({rom64x46_1_dout45__32, dc4_16_1_p1, clEXEC, stINTR, clPSWSTART, incSTRCNT}),
    .DOUT31__0({mxMAR1, mxMAR0, clSTRCNT, ldIVTP, mxPC1, ldDW7__0, ldDW15__8, stPSWSTART, ldI, rdMEM_t, incSP, mxMDR2, decSP, ldMAR, mxMAR2, ldPC, mxPC0, mxA1, mxA2, ldC, ldV, mxA0, wrGPR, mxGPR0, incMAR, mxMDR1, wrMEM_t, ldMDR, mxMDR0, ldZ, ldN, ldA}));
  ROR ror_1 (.carryROR(Signali[0]), .input_A(Akumulator), .output_A(outROR));
  // MP2_6b mp2_6b_1: pin names not known; wires that end beside it: bropr, rom64x46_1_dout45__32, mp2_6b_1_p3, kmopr_1_adr5__0, 1'b1
  or or_1 (or_1_out, bruncnd, brcnd, bropr);
  // ADD16 add16_1: pin names not known; wires that end beside it: Signali[2], Akumulator, Sabirac, in_5
  RORC rorc_1 (.PSWC(PSW[4]), .outputC(Signali[1]), .inputA(Akumulator), .outputA(outRORC));
  // SUB16 sub16_1: pin names not known; wires that end beside it: Signali[3], Akumulator, Oduzimac, 16'h1
  or or_2 (or_2_out, PSW[4], PSW[1]);
  xor xor_1 (xor_1_out, PSW[2], PSW[3]);
  not not_4 (not_4_out, PHASEFFBUS[2]);
  not not_5 (not_5_out, in_3);
  not not_6 (not_6_out, brorjmp);
  not not_7 (not_7_out, brinsttype);
  not not_8 (not_8_out, ENDOFARRAY);
  not not_9 (not_9_out, ACCEQMDR);
  or or_3 (or_3_out, xor_1_out, PSW[1]);
  and and_1 (and_1_out, not_4_out, brnotEXEC);
  and and_2 (and_2_out, ADDRBUS[6], brregdir);
  and and_3 (and_3_out, not_5_out, brnotFCBUS);
  and and_4 (and_4_out, not_6_out, brnotbrorjmp);
  and and_5 (and_5_out, not_7_out, brnotbrinsttype);
  and and_6 (and_6_out, not_8_out, brnotENDOFARRAY);
  and and_7 (and_7_out, not_9_out, brnotACCEQMDR);
  and and_8 (and_8_out, ~PSW[4], INSTRUCBUS[8]);  // AND_Gate
  and and_9 (and_9_out, PSW[4], INSTRUCBUS[9]);
  and and_10 (and_10_out, or_2_out, INSTRUCBUS[10]);
  and and_11 (and_11_out, ~or_3_out, INSTRUCBUS[11]);  // AND_Gate
  and and_12 (and_12_out, or_3_out, INSTRUCBUS[12]);
  and and_13 (brinsttype, INSTRUCBUS[2], 1'b1);
  Comparator comparator_1 (.a(in_6), .b(Akumulator[7:0]), .eq(ACCEQMDR));  // open: gt, lt
  or or_4 (brcnd, and_1_out, and_2_out, and_3_out, and_4_out, and_5_out, and_6_out, and_7_out);
  or or_5 (brorjmp, and_8_out, and_9_out, and_10_out, and_11_out, and_12_out);
  and and_14 (ENDOFARRAY, ~in_6[0], ~in_6[1], ~in_6[2], ~in_6[3], ~in_6[4], ~in_6[5], ~in_6[6], ~in_6[7]);  // AND_Gate
  assign CMEMBUS[0] = ldMAR ? 1'b1 : 1'bz;  // Controlled_Buffer controlled_buffer_1
  assign CMEMBUS[1] = incMAR ? 1'b1 : 1'bz;  // Controlled_Buffer controlled_buffer_2
  assign CMEMBUS[2] = ldMDR ? 1'b1 : 1'bz;  // Controlled_Buffer controlled_buffer_3
  assign CMEMBUS[3] = ldPC ? 1'b1 : 1'bz;  // Controlled_Buffer controlled_buffer_4
  assign CMEMBUS[5] = mxMAR0 ? 1'b1 : 1'bz;  // Controlled_Buffer controlled_buffer_5
  assign CMEMBUS[6] = mxMAR1 ? 1'b1 : 1'bz;  // Controlled_Buffer controlled_buffer_6
  assign CMEMBUS[7] = mxMDR0 ? 1'b1 : 1'bz;  // Controlled_Buffer controlled_buffer_7
  assign CMEMBUS[8] = mxMDR1 ? 1'b1 : 1'bz;  // Controlled_Buffer controlled_buffer_8
  assign CMEMBUS[9] = mxMDR2 ? 1'b1 : 1'bz;  // Controlled_Buffer controlled_buffer_9
  assign CMEMBUS[10] = mxMAR2 ? 1'b1 : 1'bz;  // Controlled_Buffer controlled_buffer_10
  assign CMEMBUS[11] = mxPC0 ? 1'b1 : 1'bz;  // Controlled_Buffer controlled_buffer_11
  assign CMEMBUS[12] = mxPC1 ? 1'b1 : 1'bz;  // Controlled_Buffer controlled_buffer_12
  assign CMEMBUS[13] = incSP ? 1'b1 : 1'bz;  // Controlled_Buffer controlled_buffer_13
  assign CMEMBUS[14] = decSP ? 1'b1 : 1'bz;  // Controlled_Buffer controlled_buffer_14
  assign CFFBUS[5] = clEXEC ? 1'b1 : 1'bz;  // Controlled_Buffer controlled_buffer_15
  assign CFFBUS[6] = stINTR ? 1'b1 : 1'bz;  // Controlled_Buffer controlled_buffer_16
  assign CPSW[0] = clPSWSTART ? 1'b1 : 1'bz;  // Controlled_Buffer controlled_buffer_17
  assign CPSW[1] = stPSWSTART ? 1'b1 : 1'bz;  // Controlled_Buffer controlled_buffer_18
  assign CPSW[2] = ldN ? 1'b1 : 1'bz;  // Controlled_Buffer controlled_buffer_19
  assign CPSW[3] = ldZ ? 1'b1 : 1'bz;  // Controlled_Buffer controlled_buffer_20
  assign CPSW[4] = ldC ? 1'b1 : 1'bz;  // Controlled_Buffer controlled_buffer_21
  assign CPSW[5] = ldV ? 1'b1 : 1'bz;  // Controlled_Buffer controlled_buffer_22
  assign CPSW[6] = ldI ? 1'b1 : 1'bz;  // Controlled_Buffer controlled_buffer_23
  assign CREGBUS[3] = wrGPR ? 1'b1 : 1'bz;  // Controlled_Buffer controlled_buffer_24
  assign CREGBUS[14] = ldDW15__8 ? 1'b1 : 1'bz;  // Controlled_Buffer controlled_buffer_25
  assign CREGBUS[15] = ldDW7__0 ? 1'b1 : 1'bz;  // Controlled_Buffer controlled_buffer_26
  assign CREGBUS[16] = ldIVTP ? 1'b1 : 1'bz;  // Controlled_Buffer controlled_buffer_27
  assign CREGBUS[17] = mxGPR0 ? 1'b1 : 1'bz;  // Controlled_Buffer controlled_buffer_28
  assign rdMEM = rdMEM_t ? 1'b1 : 1'bz;  // Controlled_Buffer controlled_buffer_29
  assign wrMEM = wrMEM_t ? 1'b1 : 1'bz;  // Controlled_Buffer controlled_buffer_30

  // Other names for the same wires on the sheet: A7__0[7:0] = A; immed = ADDRBUS[0]; memdir = ADDRBUS[1];
  //   memind = ADDRBUS[2]; regind = ADDRBUS[3]; preincr = ADDRBUS[4]; postdec = ADDRBUS[5]; regdir = ADDRBUS[6];
  //   ALU7__0[7:0] = ALU; B7__0[7:0] = B; CLK = in_2; FCBUS = in_3; HALT = INSTRUCBUS[0]; RTS = INSTRUCBUS[1];
  //   RTI = INSTRUCBUS[2]; ROR = INSTRUCBUS[3]; RORC = INSTRUCBUS[4]; PUSHPSW = INSTRUCBUS[5]; POPPSW = INSTRUCBUS[6];
  //   STIVTP = INSTRUCBUS[7]; BGREU = INSTRUCBUS[8]; BLSSU = INSTRUCBUS[9]; BLEQU = INSTRUCBUS[10];
  //   JGRT = INSTRUCBUS[11]; JLEQ = INSTRUCBUS[12]; JMP = INSTRUCBUS[13]; JSR = INSTRUCBUS[14]; LD = INSTRUCBUS[15];
  //   ST = INSTRUCBUS[16]; ADD = INSTRUCBUS[17]; DEC = INSTRUCBUS[18]; OR = INSTRUCBUS[19]; STRFIND = INSTRUCBUS[20];
  //   outA[15:0] = Akumulator; outADDACC[15:0] = Sabirac; outB[15:0] = in_5; outDECACC[15:0] = Oduzimac;
  //   outMDR[7:0] = in_6; EXEC = PHASEFFBUS[2]; PSWSTART = PSW[0]; PSWZ = PSW[1]; PSWN = PSW[2]; PSWV = PSW[3];
  //   PSWC = PSW[4]; PSWI = PSW[15]; rst = in_1; carryROR = Signali[0]; carryRORC = Signali[1];
  //   checkADDC = Signali[2]; checkDECC = Signali[3]

  // Notes on the sheet:
  //   Akumulator
  //   Operaciona jedinica
  //   Upravljacka jedinica
  //   Sabirac
  //   Dekrementer
endmodule

module INTR (
  input  in_1,
  input  in_2,
  input  in_3,
  input  [3:0] PHASEFFBUS,
  input  [20:0] INSTRUCBUS,
  input  [15:0] PSW,
  input  [3:0] intr,
  input  [15:0] in_8,
  output [15:0] ADDIVTP,
  output [1:0] UEXT1__0,
  output inta,
  output [14:0] CMEMBUS,
  output [7:0] CFFBUS,
  output [17:0] CREGBUS,
  output rdMEM,
  output wrMEM
);

  wire and_2_out, and_3_out, and_4_out, brcnd, brnotFCBUS, brnotINTR, brnotprekid, bruncnd, clINTR, decSP,
       incMAR, ldDW7__0, ldDW15__8, ldMAR, ldMDR, ldPC, mxMAR0, mxMAR2, mxMDR0, mxMDR1, mxMDR2, mxPC1,
       not_1_out, not_2_out, not_3_out, not_4_out, not_5_out, not_6_out, or_2_out, prekid, prper, rdMEM_t,
       stFETCH, wrMEM_t;
  wire [2:1] IVTDSP15__0;
  wire [4:0] rom64x26_1_dout;
  wire [5:0] reg6_inc_ld_1_a5__0;
  wire [20:18] dc3_8_1_p1;

  and and_1 (prekid, prper, PSW[15], not_2_out);
  not not_1 (not_1_out, in_1);
  // DC3_8 dc3_8_1: pin names not known; wires that end beside it: dc3_8_1_p1, 1'b1, bruncnd, brnotINTR, brnotprekid, brnotFCBUS
  not not_2 (not_2_out, INSTRUCBUS[0]);
  REG6_INC_LD reg6_inc_ld_1 (
    .I5__0({1'b0, rom64x26_1_dout}), .LD(or_2_out), .INC(not_3_out), .mr(not_1_out), .CLK(in_2),
    .A5__0(reg6_inc_ld_1_a5__0));
  ROM64x26 rom64x26_1 (
    .A5__0(reg6_inc_ld_1_a5__0), .CS(1'b1),
    .DOUT({rom64x26_1_dout, dc3_8_1_p1, clINTR, stFETCH, ldPC, mxPC1, ldDW7__0, incMAR, ldDW15__8, rdMEM_t, mxMAR0, inta, mxMDR1, mxMDR0, wrMEM_t, ldMDR, mxMDR2, decSP, ldMAR, mxMAR2}));
  or or_1 (prper, intr[3], intr[2], intr[1], intr[0]);
  or or_2 (or_2_out, bruncnd, brcnd);
  not not_3 (not_3_out, or_2_out);
  // CD4 cd4_1: pin names not known; wires that end beside it: intr[3], intr[2], intr[1], intr[0], 1'b1, UEXT1__0[1], UEXT1__0[0]
  // REG2_LD reg2_ld_1: pin names not known; wires that end beside it: in_2, UEXT1__0, IVTDSP15__0, inta
  not not_4 (not_4_out, PHASEFFBUS[3]);
  not not_5 (not_5_out, prekid);
  not not_6 (not_6_out, in_3);
  and and_2 (and_2_out, not_4_out, brnotINTR);
  and and_3 (and_3_out, not_5_out, brnotprekid);
  and and_4 (and_4_out, not_6_out, brnotFCBUS);
  // ADD16 add16_1: pin names not known; wires that end beside it: in_8, ADDIVTP, {{13{1'b0}}, IVTDSP15__0, 1'b0}, 1'b0
  or or_3 (brcnd, and_2_out, and_3_out, and_4_out);
  assign CMEMBUS[0] = ldMAR ? 1'b1 : 1'bz;  // Controlled_Buffer controlled_buffer_1
  assign CMEMBUS[1] = incMAR ? 1'b1 : 1'bz;  // Controlled_Buffer controlled_buffer_2
  assign CMEMBUS[2] = ldMDR ? 1'b1 : 1'bz;  // Controlled_Buffer controlled_buffer_3
  assign CMEMBUS[3] = ldPC ? 1'b1 : 1'bz;  // Controlled_Buffer controlled_buffer_4
  assign CMEMBUS[5] = mxMAR0 ? 1'b1 : 1'bz;  // Controlled_Buffer controlled_buffer_5
  assign CMEMBUS[7] = mxMDR0 ? 1'b1 : 1'bz;  // Controlled_Buffer controlled_buffer_6
  assign CMEMBUS[8] = mxMDR1 ? 1'b1 : 1'bz;  // Controlled_Buffer controlled_buffer_7
  assign CMEMBUS[9] = mxMDR2 ? 1'b1 : 1'bz;  // Controlled_Buffer controlled_buffer_8
  assign CMEMBUS[10] = mxMAR2 ? 1'b1 : 1'bz;  // Controlled_Buffer controlled_buffer_9
  assign CMEMBUS[12] = mxPC1 ? 1'b1 : 1'bz;  // Controlled_Buffer controlled_buffer_10
  assign CMEMBUS[14] = decSP ? 1'b1 : 1'bz;  // Controlled_Buffer controlled_buffer_11
  assign CFFBUS[0] = stFETCH ? 1'b1 : 1'bz;  // Controlled_Buffer controlled_buffer_12
  assign CFFBUS[7] = clINTR ? 1'b1 : 1'bz;  // Controlled_Buffer controlled_buffer_13
  assign CREGBUS[14] = ldDW15__8 ? 1'b1 : 1'bz;  // Controlled_Buffer controlled_buffer_14
  assign CREGBUS[15] = ldDW7__0 ? 1'b1 : 1'bz;  // Controlled_Buffer controlled_buffer_15
  assign rdMEM = rdMEM_t ? 1'b1 : 1'bz;  // Controlled_Buffer controlled_buffer_16
  assign wrMEM = wrMEM_t ? 1'b1 : 1'bz;  // Controlled_Buffer controlled_buffer_17

  // Other names for the same wires on the sheet: ldBR = inta; CLK = in_2; FCBUS = in_3; HALT = INSTRUCBUS[0];
  //   intr3__0[3:0] = intr; outIVTP[15:0] = in_8; outIVTPADD[15:0] = ADDIVTP; INTR_t = PHASEFFBUS[3]; PSWI = PSW[15];
  //   rst = in_1

  // Notes on the sheet:
  //   Operaciona jedinica
  //   Upravljacka jedinica
  //   Sabirac
endmodule

module RAM (
  input  [15:0] in_1,
  input  in_2,
  input  [7:0] in_3,
  input  in_4,
  input  in_5,
  input  in_6,
  output [7:0] out_7,
  output out_8
);

  wire and_1_out, and_2_out, CNT0, LDCNT, not_1_out, notCNT0, or_1_out, reg4_ld_sl_sr_1_p6, rsff_2_p4,
       rsff_2_p5, rsff_3_p4, sl;
  wire [3:0] CNT, LFSR;

  // RSFF rsff_1: pin names not known; wires that end beside it: 1'b0, in_2, in_6, sl
  or or_1 (or_1_out, in_4, in_5);
  // REG4_LD_SL_SR reg4_ld_sl_sr_1: pin names not known; wires that end beside it: 1'b0, 1'b0, in_2, 4'b1111, LFSR, reg4_ld_sl_sr_1_p6, sl, in_6
  // RisingEdge risingedge_1: pin names not known; wires that end beside it: or_1_out, in_2, LDCNT
  // MEM64Kx8 mem64kx8_1: pin names not known; wires that end beside it: in_1, 1'b1, in_2, in_3, out_7, in_4
  xor xor_1 (reg4_ld_sl_sr_1_p6, LFSR[2], LFSR[3]);
  and and_1 (and_1_out, CNT0, not_1_out);
  not not_1 (not_1_out, LDCNT);
  // RSFF rsff_2: pin names not known; wires that end beside it: and_1_out, in_2, LDCNT, rsff_2_p4, rsff_2_p5
  not not_2 (rsff_2_p4, in_6);
  and and_2 (and_2_out, rsff_2_p5, CNT0);
  // REG4m_DEC_LD reg4m_dec_ld_1: pin names not known; wires that end beside it: in_2, LFSR, CNT, LDCNT, notCNT0, notCNT0
  or or_2 (notCNT0, CNT[0], CNT[1], CNT[2], CNT[3]);
  // RSFF rsff_3: pin names not known; wires that end beside it: out_8, in_2, and_2_out, rsff_3_p4, out_8
  not not_3 (rsff_3_p4, in_6);
  not not_4 (CNT0, notCNT0);

  // Other names for the same wires on the sheet: ADR[15:0] = in_1; CLK = in_2; DIN[7:0] = in_3; DOUT[7:0] = out_7;
  //   fc = out_8; RDMEM = in_5; rst = in_6; WRMEM = in_4

  // Notes on the sheet:
  //   Random broj predstavlja vreme pristupa memoriji
  //   Brojac za generisanje random broja 
  //   Jedinica za generisanje function complete (fc) signala
  //   Brojac za dekrementiranje random broja
endmodule
